# Fritzing sketch infrared-3-input-selector (saved by Fritzing 0.9.3b)
breadboards: 1

parts:
  S1 = Pushbutton [package="[THT]"]
  S2 = Pushbutton [package="[THT]"]
  S3 = Pushbutton [package="[THT]"]
  S4 = Pushbutton [package="[THT]"]
  LED2 = LED - 5mm [color="Green (565nm)" package="5 mm [THT]"]
  LED6 = LED - 5mm [color="Yellow (585nm)" package="5 mm [THT]"]
  IR1 = TSOP312.., 314.. [package=THT]
  R1 = Resistor [tolerance=±5% resistance=220 package=THT]
  R2 = Resistor [tolerance=±5% resistance=220 package=THT]
  R3 = Resistor [tolerance=±5% resistance=220 package=THT]
  R4 = Resistor [tolerance=±5% resistance=220 package=THT]
  R5 = Resistor [tolerance=±5% resistance=220 package=THT]
  R6 = Resistor [tolerance=±5% resistance=10k package=THT]
  R7 = Resistor [tolerance=±5% resistance=10k package=THT]
  R8 = Resistor [tolerance=±5% resistance=10k package=THT]
  R9 = Resistor [tolerance=±5% resistance=10k package=THT]
  Raspberry_Pi_Zero1 = Raspberry Pi Zero
  LED7 = LED - 5mm [color="Green (565nm)" package="5 mm [THT]"]
  LED8 = LED - 5mm [color="Green (565nm)" package="5 mm [THT]"]
  LED9 = LED - 5mm [color="Green (565nm)" package="5 mm [THT]"]

nets:
  N1: S1.Pin_1, S1.Pin_2, R6.Pin_1, Raspberry_Pi_Zero1.GPIO18
  GND: S1.Pin_3, S1.Pin_4, S2.Pin_3, S2.Pin_4, S3.Pin_3, S3.Pin_4, S4.Pin_3, S4.Pin_4, IR1.GND, R2.Pin_1, R3.Pin_1, R4.Pin_1, R5.Pin_1, Raspberry_Pi_Zero1.GND
  N2: S2.Pin_1, S2.Pin_2, R7.Pin_1, Raspberry_Pi_Zero1.GPIO23
  N3: S3.Pin_1, S3.Pin_2, R8.Pin_1, Raspberry_Pi_Zero1.GPIO24
  N4: S4.Pin_1, S4.Pin_2, R9.Pin_1, Raspberry_Pi_Zero1.GPIO25
  N5: LED2.cathode, R3.Pin_0
  N6: LED2.anode, Raspberry_Pi_Zero1.GPIO12
  N7: LED6.anode, IR1.Vs, Raspberry_Pi_Zero1.3v3
  N8: IR1.Data, R1.Pin_0, Raspberry_Pi_Zero1.GPIO26
  N9: R2.Pin_0, LED9.cathode
  N10: R4.Pin_0, LED7.cathode
  N11: R5.Pin_0, LED8.cathode
  N12: R6.Pin_0, R7.Pin_0, R8.Pin_0, R9.Pin_0, Raspberry_Pi_Zero1.5V
  N13: Raspberry_Pi_Zero1.GPIO21, LED9.anode
  N14: Raspberry_Pi_Zero1.GPIO20, LED8.anode
  N15: Raspberry_Pi_Zero1.GPIO16, LED7.anode
